# Fritzing sketch Schaltplan Barroboter (saved by Fritzing 0.9.5d)
perfboards: 11
stripboards: 4

parts:
  Raspberry_Pi_1 = Raspberry Pi 3 [part_number=RPI-3-V1.2]
  J1 = Basic Servo  # not connected
  Power_plug1 = Power plug
  J2 = Screw terminal - 2 pins [package=THT]
  M1 = Stepper Motor - Bipolar
  Pololu_A1 = Pololu A4988 [package=SO16]
  U1 = Packages: [package=tssop28-groundpad]  # not connected
  J3 = Screw terminal - 2 pins [package=THT]
  U2 = AD584 - Pin Programmable Precision Voltage Reference [part_number=AD584]  # not connected
  J4 = Screw terminal - 2 pins [package=THT]  # not connected
  M2 = DC Motor  # not connected
  M3 = DC Motor  # not connected
  M4 = DC Motor  # not connected
  M5 = DC Motor
  M6 = DC Motor  # not connected
  M7 = DC Motor  # not connected
  M8 = DC Motor  # not connected
  J5 = Screw terminal - 2 pins [package=THT]
  J6 = Screw terminal - 2 pins [package=THT]
  J7 = Screw terminal - 2 pins [package=THT]
  J8 = Screw terminal - 2 pins [package=THT]
  J9 = Screw terminal - 2 pins [package=THT]
  J10 = Screw terminal - 2 pins [package=THT]
  J11 = Screw terminal - 2 pins [package=THT]
  J12 = Screw terminal - 2 pins [package=THT]
  J13 = Screw terminal - 2 pins [package=THT]  # not connected
  J14 = Screw terminal - 2 pins [package=THT]  # not connected
  J15 = Screw terminal - 2 pins [package=THT]  # not connected
  J16 = Screw terminal - 2 pins [package=THT]  # not connected
  J17 = Screw terminal - 2 pins [package=THT]
  J18 = Screw terminal - 2 pins [package=THT]
  S1 = Toggle Switch [package=THT]
  S2 = Toggle Switch [package=THT]
  C1 = Capacitor Polarized [package=panasonic_d]  # not connected
  LED2 = RGB LED (com. cathode, rgb) [package="5 mm [THT]"]

nets:
  N1: Raspberry_Pi_1.GPIO3, S2.L2
  N2: Raspberry_Pi_1.GPIO4, S2.L1
  N3: Raspberry_Pi_1.GPIO11, Pololu_A1.VDD
  N4: Raspberry_Pi_1.GND, Pololu_A1.ENABLE, Pololu_A1.DIR, Pololu_A1.GND#8
  N5: Raspberry_Pi_1.ID_SD, Pololu_A1.STEP
  N6: Raspberry_Pi_1.GPIO19, Raspberry_Pi_1.GPIO26, Raspberry_Pi_1.GPIO20, Raspberry_Pi_1.GPIO16
  N7: Raspberry_Pi_1.5V, S1.L1, S1.L2
  N8: Power_plug1.VCC, J2.pin2, J17.pin2
  N9: J2.pin1, J17.pin1
  N10: M1.A, Pololu_A1.2B
  N11: M1.C, Pololu_A1.2A
  N12: M1.B, Pololu_A1.1A
  N13: M1.D, Pololu_A1.1B
  N14: Pololu_A1.GND#14, J12.pin1, J18.pin1
  N15: Pololu_A1.VMOT, J12.pin2, J18.pin2
  N16: J3.pin1, J3.pin2
  N17: M5.pin_1, J5.pin2, J6.pin2, J7.pin2, J8.pin2, J9.pin2, J10.pin2, J11.pin2
  N18: M5.pin_2, J5.pin1, J6.pin1, J7.pin1, J8.pin1, J9.pin1, J10.pin1, J11.pin1
  N19: LED2.red_anode, LED2.common_cathode, LED2.blue_anode

notes:
  GND
  VCC
  SDA
  SCL
  Stepper Controller
  DIR
  STEP
  EN (GND)
  PWM Controller
  5V
  SCLK
  DT
  LAN Cable
  Scale
  Splitter Board
  Scale Controller
  PWM
  Cable bundle
  12V 3A PSU Input
  12V
  12V In for Pump Controllers
  GND for Pump Controllers
  12V In for Pumps
  GND for Pumps
  12V Out
  5V Out
  VRM
  L Switch
  R Switch
  Big Pumps
  Small Pumps
  Raspberry Pi
  Stepper Motor
  5V In for Pi
  GND for Pi
  NC
  100µF Capacitor
  5V to Pi
  GND to Pi
  12V to VRM
  GND to VRM
  1 2
  3 4
  5 6
  7 8
  11 12
  9 10
  13 14
  33 34
  15 16
  17 18
  19 20
  21 22
  23 24
  25 26
  27 28
  29 30
  31 32
  35 36
  39 40
  37 38
  Micro USB Connetor
  Port 1
  LED Strip
  Port 15
  Port 8
